# Fritzing sketch Circuit (saved by Fritzing 0.9.3b)
breadboards: 4

parts:
  U1 = POT [package=pot_mammoth]
  U2 = POT [package=pot_mammoth]
  U3 = POT [package=pot_mammoth]
  T1 = LM34 Temperature Sensor [package="TO92 [THT]"]
  U4 = POT [package=pot_mammoth]
  J1 = Basic Servo
  LED1 = RGB LED (com. cathode, rbg) [package="5 mm [THT]"]
  LED3 = smd LED [color="Red (633nm)" package="0805 [SMD]"]
  S1 = Pushbutton [package="[THT]"]
  LED4 = smd LED [color="Red (633nm)" package="0805 [SMD]"]
  S2 = Pushbutton [package="[THT]"]
  LED5 = smd LED [color="Red (633nm)" package="0805 [SMD]"]
  S3 = Pushbutton [package="[THT]"]
  S4 = Pushbutton [package="[THT]"]
  LED7 = smd LED [color="Red (633nm)" package="0805 [SMD]"]
  S5 = Pushbutton [package="[THT]"]
  S6 = Pushbutton [package="[THT]"]
  LED11 = RGB LED (com. cathode, rbg) [package="5 mm [THT]"]
  LED14 = RGB LED (com. cathode, rbg) [package="5 mm [THT]"]
  R2 = Resistor [tolerance=±5% resistance=220 package="2010 [SMD]"]
  R3 = Resistor [tolerance=±5% resistance=220 package="2010 [SMD]"]
  R4 = Resistor [tolerance=±5% resistance=220 package="2010 [SMD]"]
  R5 = Resistor [tolerance=±5% resistance=220 package="2010 [SMD]"]
  R6 = Resistor [tolerance=±5% resistance=220 package="2010 [SMD]"]
  R8 = Resistor [tolerance=±5% resistance=220 package="2010 [SMD]"]
  R9 = Resistor [tolerance=±5% resistance=220 package="2010 [SMD]"]
  R10 = Resistor [tolerance=±5% resistance=220 package="2010 [SMD]"]
  R11 = Resistor [tolerance=±5% resistance=220 package="2010 [SMD]"]
  R12 = Resistor [tolerance=±5% resistance=220 package="2010 [SMD]"]
  R1 = Photocell (LDR) [package=THT]
  R13 = Resistor [tolerance=±5% resistance=220 package="2010 [SMD]"]
  R14 = Resistor [tolerance=±5% resistance=220 package="2010 [SMD]"]
  Part2 = Arduino Mega ADK (Rev3)

nets:
  VCC: U1.S, U2.S, U3.S, U4.S, J1.vcc, S1.Pin_1, S1.Pin_2, S2.Pin_1, S2.Pin_2, S3.Pin_2, S4.Pin_1, S4.Pin_2, S5.Pin_2, R1.pin_1, Part2.5V
  N1: U1.A, Part2.A0
  GND: U1.E, U2.E, U3.E, T1.+Vs, T1.GND, U4.E, J1.gnd, LED5.anode, LED7.anode, LED11.common_cathode, LED14.common_cathode, R5.Pin_0, R6.Pin_0, R8.Pin_0, R9.Pin_0, R10.Pin_0, R11.Pin_0, R12.Pin_0, R13.Pin_0, R14.Pin_0, Part2.GND
  N2: U2.A, Part2.A1
  N3: U3.A, Part2.A2
  N4: T1.Vout, Part2.A3
  N5: U4.A, Part2.A4
  N6: J1.pulse, Part2.D44
  N7: LED1.red_anode, R2.Pin_1
  N8: LED1.blue_anode, R4.Pin_1
  N9: LED1.green_anode, R3.Pin_1
  N10: LED3.cathode, Part2.D30
  N11: LED3.anode, R9.Pin_1
  N12: S1.Pin_3, S1.Pin_4, R5.Pin_1, Part2.D28
  N13: LED4.cathode, Part2.D32
  N14: LED4.anode, R8.Pin_1
  N15: S2.Pin_3, S2.Pin_4, R6.Pin_1, Part2.D34
  N16: LED5.cathode, Part2.D48
  N17: S3.Pin_3, S3.Pin_4, R11.Pin_1, Part2.D46
  N18: S4.Pin_3, S4.Pin_4, R10.Pin_1, Part2.D36
  N19: LED7.cathode, Part2.D49
  N20: S5.Pin_3, S5.Pin_4, R14.Pin_1, Part2.D47
  N21: S6.Pin_3, S6.Pin_4, R13.Pin_1, Part2.D45
  N22: LED11.red_anode, Part2.D38
  N23: LED11.blue_anode, Part2.D40
  N24: LED11.green_anode, Part2.D42
  N25: LED14.red_anode, Part2.D43
  N26: LED14.blue_anode, Part2.D41
  N27: LED14.green_anode, Part2.D39
  N28: R2.Pin_0, Part2.D7_PWM
  N29: R3.Pin_0, Part2.D5_PWM
  N30: R4.Pin_0, Part2.D6_PWM
  N31: R12.Pin_1, R1.pin_0, Part2.A5
